# Fritzing sketch main (saved by Fritzing 0.9.6b)
breadboards: 1

parts:
  PIC_16F877A1 = PIC 16F877A [package=THT]
  R1 = Resistor [tolerance=±5% power=0.25 resistance=220 package=THT]
  R2 = Resistor [tolerance=±5% power=0.25 resistance=220 package=THT]
  LED1 = LED - 5mm [color="Green (555nm)" current=0.030 package="5 mm [THT]"]
  LED2 = LED - 5mm [color="Red (633nm)" current=0.030 package="5 mm [THT]"]
  C1 = Ceramic Capacitor [capacitance=100nF voltage=35V package="100 mil [THT, multilayer]"]
  R3 = Resistor [tolerance=±5% power=0.25 resistance=1k package=THT]
  S1 = Pushbutton [package="[THT]"]

nets:
  N1: PIC_16F877A1.VSS#30, R1.Pin_1, R2.Pin_1, C1.0, R3.Pin_1
  N2: PIC_16F877A1.VDD#31, PIC_16F877A1.RB0/INT, C1.1, R3.Pin_0, S1.Pin_1, S1.Pin_2, S1.Pin_3, S1.Pin_4
  N3: PIC_16F877A1.RB1, LED1.anode
  N4: PIC_16F877A1.RB2, LED2.anode
  N5: R1.Pin_0, LED2.cathode
  N6: R2.Pin_0, LED1.cathode
